// Logisim project somador-subtrator .circ as structural Verilog: 4 circuits, main circuit main
module main (
);

  wire full4bit_1_c4;
  wire [2:0] full4bit_1_s0;
  wire [3:0] xor_1_out;
  wire [3:3] full4bit_1_s3;

  Hex_Digit_Display hex_digit_display_1 (.value(4'b0010));  // open: dp
  Hex_Digit_Display hex_digit_display_2 (.value(4'b0001));  // open: dp
  assign xor_1_out = 4'b1111 ^ 4'b0010;  // XOR_Gate xor_1, 4 bits wide
  full4bit full4bit_1 (
    .co(1'b1), .in_2(xor_1_out), .in_3(4'b0001), .s0(full4bit_1_s0[0]), .s1(full4bit_1_s0[1]),
    .s2(full4bit_1_s0[2]), .s3(full4bit_1_s3[3]), .c4(full4bit_1_c4));
  LED led_1 (.in(full4bit_1_c4));
  Hex_Digit_Display hex_digit_display_3 (.value({full4bit_1_s3[3], full4bit_1_s0}));  // open: dp
  LED led_2 (.in(full4bit_1_s3[3]));
  LED led_3 (.in(full4bit_1_s0[2]));
  LED led_4 (.in(full4bit_1_s0[0]));
  LED led_5 (.in(full4bit_1_s0[1]));
  LED led_6 (.in(full4bit_1_s3[3]));
  Hex_Digit_Display hex_digit_display_4 (.value({1'b0, full4bit_1_s0}));  // open: dp

  // Notes on the sheet:
  //   operando B
  //   operando A
  //   resultado = A {+,-} B
  //   0:soma; 1: subtrai
  //   resultado
endmodule

module half (
  input  a,
  input  b,
  output s,
  output co
);

  and and_1 (co, a, b);
  xor xor_1 (s, a, b);
endmodule

module full (
  input  ci,
  input  a,
  input  b,
  output s,
  output co
);

  wire half_1_co, half_1_s, half_2_co;

  half half_1 (.a(a), .b(b), .s(half_1_s), .co(half_1_co));
  half half_2 (.a(ci), .b(half_1_s), .s(s), .co(half_2_co));
  or or_1 (co, half_2_co, half_1_co);
endmodule

module full4bit (
  input  co,
  input  [3:0] in_2,
  input  [3:0] in_3,
  output s0,
  output s1,
  output s2,
  output s3,
  output c4
);

  wire full_1_co, full_2_co, full_3_co;

  Hex_Digit_Display hex_digit_display_1 (.value(in_2));  // open: dp
  Hex_Digit_Display hex_digit_display_2 (.value(in_3));  // open: dp
  full full_1 (.ci(co), .a(in_2[0]), .b(in_3[0]), .s(s0), .co(full_1_co));
  full full_2 (.ci(full_1_co), .a(in_2[1]), .b(in_3[1]), .s(s1), .co(full_2_co));
  full full_3 (.ci(full_2_co), .a(in_2[2]), .b(in_3[2]), .s(s2), .co(full_3_co));
  full full_4 (.ci(full_3_co), .a(in_2[3]), .b(in_3[3]), .s(s3), .co(c4));
  Hex_Digit_Display hex_digit_display_3 (.value({s3, s2, s1, s0}));  // open: dp
endmodule
